// Logisim project Que 1.circ as structural Verilog: 1 circuit, main circuit main
module main (
  input  A,
  input  B,
  input  C,
  input  D,
  output Y
);

  wire and_1_out, and_2_out, and_3_out, not_1_out, not_2_out;

  not not_1 (not_1_out, D);
  not not_2 (not_2_out, D);
  and and_1 (and_1_out, A, B, not_1_out);
  and and_2 (and_2_out, B, not_2_out);
  and and_3 (and_3_out, A, C);
  or or_1 (Y, and_1_out, and_2_out, and_3_out, C);

  // Notes on the sheet:
  //   Input
  //   E22CSEU0752
  //   Harsh Panwar
  //   Output
endmodule
