// Logisim project Que 2.circ as structural Verilog: 1 circuit, main circuit main
module main (
  input  A,
  input  B,
  input  C,
  input  D,
  input  E,
  output Y
);

  wire nor_1_out, or_1_out, or_2_out;

  or or_1 (or_1_out, A, B);
  or or_2 (or_2_out, C, D, E);
  nor nor_1 (nor_1_out, A, D);
  and and_1 (Y, or_1_out, or_2_out, nor_1_out);

  // Notes on the sheet:
  //   Input
  //   E22CSEU0752
  //   Harsh Panwar
  //   Output
endmodule
