// Logisim project Que 3.circ as structural Verilog: 1 circuit, main circuit main
module main (
  input  S0,
  input  S1,
  input  S2,
  input  A0,
  input  A1,
  input  A2,
  input  A3,
  input  A4,
  input  A5,
  input  A6,
  input  A7,
  input  S3,
  output Y
);

  wire and_1_out, and_2_out, and_3_out, and_4_out, and_5_out, and_6_out, and_7_out, and_8_out, not_1_out,
       not_2_out, not_3_out, not_4_out, not_5_out, not_6_out, not_7_out, not_8_out, not_9_out, not_10_out,
       not_11_out, not_12_out;

  not not_1 (not_1_out, S0);
  not not_2 (not_2_out, S1);
  not not_3 (not_3_out, S2);
  not not_4 (not_4_out, S1);
  not not_5 (not_5_out, S2);
  not not_6 (not_6_out, S0);
  not not_7 (not_7_out, S2);
  not not_8 (not_8_out, S2);
  not not_9 (not_9_out, S0);
  not not_10 (not_10_out, S1);
  not not_11 (not_11_out, S1);
  not not_12 (not_12_out, S0);
  and and_1 (and_1_out, not_1_out, not_2_out, not_3_out, A0);
  and and_2 (and_2_out, S0, not_4_out, not_5_out, A1);
  and and_3 (and_3_out, not_6_out, S1, not_7_out, A2);
  and and_4 (and_4_out, S0, S1, not_8_out, A3);
  and and_5 (and_5_out, not_9_out, not_10_out, S2, A4);
  and and_6 (and_6_out, S0, not_11_out, S2, A5);
  and and_7 (and_7_out, not_12_out, S1, S2, A6);
  and and_8 (and_8_out, S0, S1, S3, A7);
  or or_1 (Y, and_1_out, and_2_out, and_3_out, and_4_out, and_5_out, and_6_out, and_7_out, and_8_out);

  // Notes on the sheet:
  //   Input
  //   E22CSEU0752
  //   Harsh Panwar
  //   8X1 Mux
  //   Output
endmodule
