// Logisim project Que 4.circ as structural Verilog: 1 circuit, main circuit main
module main (
  input  A,
  input  B,
  output Y
);

  wire nand_1_out, nand_2_out, nand_3_out;

  nand nand_1 (nand_1_out, A, B);
  nand nand_2 (nand_2_out, A, nand_1_out);
  nand nand_3 (nand_3_out, nand_1_out, B);
  nand nand_4 (Y, nand_2_out, nand_3_out);

  // Notes on the sheet:
  //   Input
  //   E22CSEU0752
  //   Harsh Panwar
  //   XOR gate using NAND Gate
  //   Output
endmodule
