// Logisim project Que 5.circ as structural Verilog: 1 circuit, main circuit main
module main (
  input  A,
  input  B,
  input  in_3,
  input  in_4,
  output Y,
  output Output
);

  wire and_1_out, nand_1_out, nor_1_out, nor_2_out, nor_3_out;

  nor nor_1 (nor_1_out, in_3, in_4);
  nand nand_1 (nand_1_out, A, B);
  and and_1 (and_1_out, A, B);
  nor nor_2 (nor_2_out, in_3, nor_1_out);
  nor nor_3 (nor_3_out, nor_1_out, in_4);
  or or_1 (Y, nand_1_out, and_1_out);
  nor nor_4 (Output, nor_2_out, nor_3_out);

  // Notes on the sheet:
  //   Input
  //   Input
  //   XNOR gate using basic gates
  //   XNOR gate using NOR gates
  //   E22CSEU0752
  //   Harsh Panwar
  //   Output
endmodule
